# Fritzing sketch carbot (saved by Fritzing 0.9.3b)
circuit board: 9.7cm x 7.5cm
breadboards: 1

parts:
  M1 = ESP32S-HiLetgo [part_number=ESP32S-HiLetgo]
  OV_7670 = female pin header, 18 pins [form="♀ (female)"]
  L298N = female pin header, 8 pins [form="♀ (female)"]
  Inverter = 74HC04_HEX_INVERTER [package=dil14]
  Q1 = NPN-Transistor [package="TO92 [THT]"]
  R1 = Resistor [tolerance=±5% resistance=220 package=THT]
  R2 = Resistor [tolerance=±5% resistance=220 package=THT]
  J2 = double row female pin header, 4 pins [form="♀ (female)"]
  +12 = female pin header, 1 pin [form="♀ (female)"]
  GND = female pin header, 1 pin [form="♀ (female)"]
  OUT+_(5V) = female pin header, 1 pin [form="♀ (female)"]
  IN+ = female pin header, 1 pin [form="♀ (female)"]
  IN- = female pin header, 1 pin [form="♀ (female)"]
  OUT- = female pin header, 1 pin [form="♀ (female)"]

nets:
  N1: M1.3.3, OV_7670.pin2, OV_7670.pin18
  N2: M1.GPIO32, R1.Pin_1
  N3: M1.GPIO33, L298N.pin8
  N4: M1.GPIO25, L298N.pin7, Inverter.1A
  N5: M1.GPIO26, L298N.pin5, Inverter.2A
  N6: M1.GPIO27, L298N.pin3
  N7: M1.GPIO14, OV_7670.pin5
  N8: M1.GPIO12, OV_7670.pin4
  GND: M1.GND, OV_7670.pin1, OV_7670.pin17, L298N.pin2, Inverter.GND, Q1.E, R2.Pin_1, GND.pin1, IN-.pin1, OUT-.pin1
  N9: M1.GPIO13, OV_7670.pin3
  VIN: M1.VIN, Inverter.VCC, OUT+_(5V).pin1
  N10: M1.GPIO15, OV_7670.pin6
  N11: M1.GPIO2, OV_7670.pin7
  N12: M1.GPIO0, OV_7670.pin8
  N13: M1.GPIO4, OV_7670.pin9
  N14: M1.GPIO16, OV_7670.pin10
  N15: M1.GPIO17, OV_7670.pin11
  N16: M1.GPIO5, OV_7670.pin12
  N17: M1.GPIO18, OV_7670.pin13
  N18: M1.GPIO19, OV_7670.pin14
  N19: M1.GPIO21, OV_7670.pin15
  N20: M1.GPIO22, OV_7670.pin16
  N21: L298N.pin1, J2.pin1, J2.pin2, +12.pin1, IN+.pin1
  N22: L298N.pin4, Inverter.2Y
  N23: L298N.pin6, Inverter.1Y
  N24: Q1.B, R1.Pin_0, R2.Pin_0
  N25: Q1.C, J2.pin3, J2.pin4

notes:
  3v3  SCK  VS  PLK  D7   D5  D3   D1  RST
  GND  SDA  HS  XCK  D6  D4   D2  D0   PWD
  -+

custom parts:
  ESP32S-HiLetgo: HiLetgo ESP-WROOM-32 ESP32 ESP-32S Development Board 2.4GHz Dual-Mode WiFi + Bluetooth Dual Cores Microcontroller The ESP32 integrated with Antenna switches, RF Balun, power amplifiers, low-noise amplifiers, filters, and management modules, and the entire solution occupies the least area of PCB. 2.4 GHz Wi-Fi plus Bluetooth dual-mode chip, with TSMC Ultra-low power consumption 40nm technology,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
